# Fritzing sketch arduino-metronome (saved by Fritzing 0.9.4)
breadboards: 2

parts:
  R1 = Rotary Potentiometer (Small) [maximum_resistance=100kΩ package=THT]
  R2 = Rotary Potentiometer (Small) [maximum_resistance=100kΩ package=THT]
  LCD1 = LCD screen
  J1 = Piezo Speaker
  LED1 = RGB LED (com. cathode, rgb) [package="5 mm [THT]"]
  Part1 = Arduino Mega ADK (Rev3)
  7_Segment1 = 7 Segment Display
  R3 = Resistor [tolerance=±5% resistance=4.7k package=THT]
  R4 = Resistor [tolerance=±5% resistance=330 package=THT]
  R5 = Resistor [tolerance=±5% resistance=330 package=THT]
  R6 = Resistor [tolerance=±5% resistance=330 package=THT]
  R7 = Resistor [tolerance=±5% resistance=330 package=THT]
  R8 = Resistor [tolerance=±5% resistance=330 package=THT]
  R9 = Resistor [tolerance=±5% resistance=330 package=THT]
  R10 = Resistor [tolerance=±5% resistance=330 package=THT]
  R11 = Resistor [tolerance=±5% resistance=330 package=THT]
  R12 = Resistor [tolerance=±5% resistance=330 package=THT]
  R13 = Resistor [tolerance=±5% resistance=330 package=THT]

nets:
  VSS: R1.leg1, R2.leg1, LCD1.VSS, LCD1.R/W, LCD1.LED-, J1.pin1, LED1.common_cathode, Part1.GND, 7_Segment1.common_cathode, R3.Pin_0
  N1: R1.wiper, Part1.A7
  VDD: R1.leg2, R2.leg2, LCD1.VDD, Part1.5V
  N2: R2.wiper, Part1.A1
  N3: LCD1.V0, R3.Pin_1
  N4: LCD1.RS, Part1.D4_PWM
  N5: LCD1.E, Part1.D6_PWM
  N6: LCD1.DB4, Part1.D10_PWM
  N7: LCD1.DB5, Part1.D11_PWM
  N8: LCD1.DB6, Part1.D12_PWM
  N9: LCD1.DB7, Part1.D13_PWM
  N10: LCD1.LED+, Part1.3V3
  N11: J1.pin2, Part1.D52/SCK
  N12: LED1.red_anode, R4.Pin_0
  N13: LED1.green_anode, R5.Pin_0
  N14: LED1.blue_anode, R6.Pin_0
  N15: Part1.D23, R7.Pin_1
  N16: Part1.D24, R8.Pin_0
  N17: Part1.D25, R9.Pin_0
  N18: Part1.D26, R13.Pin_0
  N19: Part1.D27, R12.Pin_0
  N20: Part1.D28, R10.Pin_1
  N21: Part1.D29, R11.Pin_1
  N22: Part1.D36, R4.Pin_1
  N23: Part1.D37, R5.Pin_1
  N24: Part1.D38, R6.Pin_1
  N25: 7_Segment1.Segment_E, R9.Pin_1
  N26: 7_Segment1.Segment_D, R8.Pin_1
  N27: 7_Segment1.Segment_C, R7.Pin_0
  N28: 7_Segment1.Segment_B, R11.Pin_0
  N29: 7_Segment1.Segment_A, R10.Pin_0
  N30: 7_Segment1.Segment_F, R12.Pin_1
  N31: 7_Segment1.Segment_G, R13.Pin_1
